# Fritzing sketch press_sensor (saved by Fritzing 0.9.2b)
breadboards: 1

parts:
  パーツ1 = Arduino Board Ethernet
  J1 = Basic Force Sensing Resistor (FSR) [package=THT]
  R1 = Resistor [tolerance=±5% resistance=220 package=THT]  # not connected

nets:
  N1: パーツ1.A3, J1.pin_0
  N2: パーツ1.5V, J1.pin_1
