# Fritzing sketch servomotor (saved by Fritzing 0.9.2b)
breadboards: 1

parts:
  Raspberry_Pi1 = Raspberry Pi B rev2  # not connected
  パーツ1 = Arduino Uno (Rev3)
  J1 = Basic Servo

nets:
  N1: パーツ1.D11_PWM/MOSI, J1.gnd
  5V: パーツ1.5V, J1.vcc
  N2: パーツ1.GND, J1.pulse
